# Fritzing sketch BlobsterWiringmicroSD (saved by Fritzing 0.9.9b)

parts:
  Power_plug1 = Power plug
  J1 = Basic Servo
  J2 = Basic Servo
  U1 = LM2596 step down module
  OLED_I2C1 = OLED 128x64 I2C Monochrome Display
  J3 = Basic Servo
  R1 = Resistor [tolerance=±5% power=0.25 resistance=220 package=THT]
  R2 = Resistor [tolerance=±5% power=0.25 resistance=220 package=THT]
  J4 = JST-B3P-VH [part_number=JST-B3P-VH package=THT]
  Součástka2 = Arduino Nano Every
  Mod1 = Full Size SD Card Module

nets:
  GND: Power_plug1.GND, J1.gnd, J2.gnd, U1.IN-, U1.OUT-, OLED_I2C1.GND, J3.gnd, R2.Pin_1, J4.pin1, Součástka2.GND, Součástka2.D13~, Mod1.pin_2, Mod1.pin_11, Mod1.pin_15
  VCC: Power_plug1.VCC, U1.IN+, J4.pin3, Součástka2.VIN
  VCC_2: J1.vcc, J2.vcc, U1.OUT+, J3.vcc
  N1: J1.pulse, Součástka2.D6~
  N2: J2.pulse, Součástka2.D5~
  N3: OLED_I2C1.SDA, Součástka2.A4
  N4: OLED_I2C1.SCK, Součástka2.A5
  VDD: OLED_I2C1.VDD, Součástka2.D11/MOSI, Součástka2.+5V, Mod1.pin_9
  N5: J3.pulse, Součástka2.D3~
  N6: R1.Pin_0, Součástka2.D4
  N7: R1.Pin_1, R2.Pin_0, J4.pin2
  N8: Součástka2.D10~, Mod1.pin_7
  N9: Součástka2.D12~/MISO, Mod1.pin_13
  N10: Součástka2.3V3, Mod1.pin_5

custom parts:
  LM2596 step down module: LM2596 DC-DC step down power supply module 3 A.
  Arduino Nano Every: The Nano Every is Arduino’s 5V compatible board in the smallest available form factor: 45x18mm! The Arduino Nano is the preferred board for many projects requiring a small and easy to use microcontroller board. The small footprint and low price, make the Nano Every particularly suited for wearable inventions, low cost robotics, electronic musical instruments, and general use to control smaller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
  Full Size SD Card Module: SD Card Module Slot Socket Reader For Arduino ARM MCU
